# Fritzing sketch NetduinoGPS (saved by Fritzing 0.9.2b)

parts:
  Netduino1 = Netduino
  Nokia_5110_LCD = Nokia5110LCDModule
  GY-GPS6MV1 = GY-GPS6MV1 [package=sup500f]

nets:
  N1: Netduino1.D13_SPCK, Nokia_5110_LCD.SCLK
  N2: Netduino1.D11_MOSI, Nokia_5110_LCD.6_DN_(MOSI)
  N3: Netduino1.D10_PWM3, Nokia_5110_LCD.SCE
  N4: Netduino1.D9_PWM2, Nokia_5110_LCD.LED
  N5: Netduino1.D8_CTS1, Nokia_5110_LCD.D/C
  N6: Netduino1.D7_RTS1, Nokia_5110_LCD.RST
  N7: Netduino1.D1_TX0, GY-GPS6MV1.RX
  N8: Netduino1.D0_RX0, GY-GPS6MV1.TX
  VCC: Netduino1.3V3, Nokia_5110_LCD.Vcc, GY-GPS6MV1.VCC
  N9: Netduino1.GND#19, GY-GPS6MV1.GND
  N10: Netduino1.GND#20, Nokia_5110_LCD.Grnd

notes:
  GND TX RX VCC
  1 2 3 4 5 6 7 8

custom parts:
  : Nokia 5110 LCD with 8 pin. It's a 45mm*45mm module part. Description: The Nokia 5110 is a basic graphic LCD screen for lots of applications. It was originally intended for as a cell phone screen. This one is mounted on an easy to solder PCB. It uses the PCD8544 controller. The PCD8544 is a low power CMOS LCD controller/driver, designed to drive a graphic display of 48 rows and 84 columns. All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
  GY-GPS6MV1: NEO GPS
